// Logisim project Aula02.circ as structural Verilog
module Add_4 (
  input  [3:0] in_1,
  input  [3:0] in_2,
  input  in_3,
  output out_4,
  output [3:0] out_5
);

  wire add_1_2_out_4, add_1_3_out_4, add_1_4_out_4;

  Add_1 add_1_1 (.in_1(in_2[3]), .in_2(in_1[3]), .Vem_1(add_1_2_out_4), .out_4(out_4), .out_5(out_5[3]));
  Add_1 add_1_2 (.in_1(in_2[2]), .in_2(in_1[2]), .Vem_1(add_1_3_out_4), .out_4(add_1_2_out_4), .out_5(out_5[2]));
  Add_1 add_1_3 (.in_1(in_2[1]), .in_2(in_1[1]), .Vem_1(add_1_4_out_4), .out_4(add_1_3_out_4), .out_5(out_5[1]));
  Add_1 add_1_4 (.in_1(in_2[0]), .in_2(in_1[0]), .Vem_1(in_3), .out_4(add_1_4_out_4), .out_5(out_5[0]));
endmodule

module Add_1 (
  input  in_1,
  input  in_2,
  input  Vem_1,
  output out_4,
  output out_5
);

  wire and_1_out, and_2_out, or_1_out, xor_1_out;

  xor xor_1 (xor_1_out, in_1, in_2);
  or or_1 (or_1_out, in_2, in_2);
  xor xor_2 (out_4, xor_1_out, Vem_1);
  and and_1 (and_1_out, or_1_out, in_1);
  and and_2 (and_2_out, in_2, Vem_1);
  or or_2 (out_5, and_1_out, and_2_out);
endmodule

module Sub_1 (
  input  A,
  input  B,
  input  C_in,
  output out_4,
  output out_5
);

  wire and_1_out, and_2_out, not_1_out, or_1_out, xor_1_out;

  not not_1 (not_1_out, A);
  xor xor_1 (xor_1_out, A, B);
  or or_1 (or_1_out, B, C_in);
  xor xor_2 (out_4, xor_1_out, C_in);
  and and_1 (and_1_out, or_1_out, not_1_out);
  and and_2 (and_2_out, B, C_in);
  or or_2 (out_5, and_1_out, and_2_out);
endmodule

module Sub_4 (
  input  [3:0] A,
  input  [3:0] B,
  input  C_in,
  output C_out,
  output [3:0] out_5
);

  wire sub_1_2_out_5, sub_1_3_out_5, sub_1_4_out_5;

  Sub_1 sub_1_1 (.A(A[3]), .B(B[3]), .C_in(sub_1_2_out_5), .out_4(out_5[3]), .out_5(C_out));
  Sub_1 sub_1_2 (.A(A[2]), .B(B[2]), .C_in(sub_1_3_out_5), .out_4(out_5[2]), .out_5(sub_1_2_out_5));
  Sub_1 sub_1_3 (.A(A[1]), .B(B[1]), .C_in(sub_1_4_out_5), .out_4(out_5[1]), .out_5(sub_1_3_out_5));
  Sub_1 sub_1_4 (.A(A[0]), .B(B[0]), .C_in(C_in), .out_4(out_5[0]), .out_5(sub_1_4_out_5));
endmodule
